# Fritzing sketch RXShield (saved by Fritzing 0.9.2b)
circuit board: 6.88566cm x 5.36311cm
breadboards: 1

parts:
  Arduino = Arduino Uno (Rev3)
  PROGRAM = Pushbutton [package="[THT]"]
  RESET = Pushbutton [package="[THT]"]
  RX = female pin header, 4 pins [form="♀ (female)"]
  10k = Resistor [tolerance=±5% resistance=10k package=THT]

nets:
  N1: Arduino.GND, RESET.Pin_3, RX.pin1, 10k.Pin_1
  N2: Arduino.D2, PROGRAM.Pin_3, PROGRAM.Pin_4, 10k.Pin_0
  N3: Arduino.D3_PWM, RX.pin3
  N4: Arduino.RESET, RESET.Pin_1, RESET.Pin_2
  N5: Arduino.5V, PROGRAM.Pin_1, PROGRAM.Pin_2, RX.pin4

notes:
  GND
  DATA
  VCC
  PROGRAM:
  RX:
  RXShield, RX shield for Arduino UNO, v0.1
